# Fritzing sketch skymonitor-v3 (saved by Fritzing 1.0.6)

parts:
  Part1 = Arduino Nano (Rev3.0)
  U1 = ESP8266 WiFi Module [part_number=ESP8266]
  YL-83_-_Detection_Board2 = YL-83 Rain Sensor - Detection Board
  U2 = MLX90614 [package=to-39]
  Light_Sensor1 = Light Sensor
  YL-83_-_Control_Board2 = YL-83 Rain Sensor - Control Board
  Light_Sensor2 = Light Sensor

nets:
  N1: Part1.D0/RX, U1.TXD
  N2: Part1.D3, YL-83_-_Control_Board2.DO
  GND: Part1.GND, Light_Sensor1.GND, YL-83_-_Control_Board2.GND
  5V: Part1.5V, Light_Sensor1.Vcc
  N3: Part1.A5, Light_Sensor1.SCL
  N4: Part1.A4, Light_Sensor1.SDA
  N5: Part1.A0, YL-83_-_Control_Board2.AO
  3V3: Part1.3V3, YL-83_-_Control_Board2.VCC
  VSS: U1.GPIO_15, U2.VSS, Light_Sensor2.GND
  N6: U1.GPIO_4, U2.PWM_SDA, Light_Sensor2.SDA
  N7: U1.GPIO_5, U2.SCL_VZ, Light_Sensor2.SCL
  VDD: U1.GPIO_13, U2.VDD, Light_Sensor2.Vcc
  N8: YL-83_-_Detection_Board2.POS, YL-83_-_Control_Board2.POS
  N9: YL-83_-_Detection_Board2.NEG, YL-83_-_Control_Board2.NEG

custom parts:
  YL-83 Rain Sensor - Detection Board: The YL-83 is a rain sensor that has more resistance when dry and less resistance when wet. The module runs at 5V.
  YL-83 Rain Sensor - Control Board: The YL-83 is a rain sensor that has more resistance when dry and less resistance when wet. The module runs at 5V.
