# Fritzing sketch rainSensor (saved by Fritzing 0.9.4)
circuit board: 8.46667cm x 5.64444cm
breadboards: 1

parts:
  Rapb_zero = Raspberry Pi Zero
  MCP3008 = MCP3008 [package=dil16]
  YL-83_-_Control_Board1 = YL-83 Rain Sensor - Control Board
  YL-83_-_Detection_Board1 = YL-83 Rain Sensor - Detection Board
  Power = HLK-PM01

nets:
  VDD: Rapb_zero.pin_1, Rapb_zero.pin_3, Rapb_zero.pin_17, MCP3008.VREF, MCP3008.VDD, YL-83_-_Control_Board1.VCC
  N1: Rapb_zero.pin_2, Rapb_zero.pin_4, Power.+Vo
  N2: Rapb_zero.pin_6, Rapb_zero.pin_8, Rapb_zero.pin_9, Rapb_zero.pin_23, Rapb_zero.pin_25, Rapb_zero.pin_39, MCP3008.DGND, MCP3008.CLK, MCP3008.AGND, YL-83_-_Control_Board1.GND, Power.-Vo
  N3: Rapb_zero.pin_19, MCP3008.Din
  N4: Rapb_zero.pin_21, MCP3008.Dout
  N5: Rapb_zero.pin_24, MCP3008.CS/SHDN
  N6: MCP3008.CH0, YL-83_-_Control_Board1.AO
  N7: YL-83_-_Control_Board1.POS, YL-83_-_Detection_Board1.POS
  N8: YL-83_-_Control_Board1.NEG, YL-83_-_Detection_Board1.NEG

custom parts:
  YL-83 Rain Sensor - Control Board: The YL-83 is a rain sensor that has more resistance when dry and less resistance when wet. The module runs at 5V.
  YL-83 Rain Sensor - Detection Board: The YL-83 is a rain sensor that has more resistance when dry and less resistance when wet. The module runs at 5V.
