# Fritzing sketch skymonitor-a (saved by Fritzing 0.9.3b)

parts:
  Part1 = Arduino Nano (Rev3.0)
  U1 = ESP8266 WiFi Module [part_number=ESP8266]
  YL-83_-_Detection_Board2 = YL-83 Rain Sensor - Detection Board
  U2 = MLX90614 [package=to-39]
  Light_Sensor1 = Light Sensor
  YL-83_-_Control_Board2 = YL-83 Rain Sensor - Control Board
  LED1 = smd LED [color="Red (633nm)" package="0603 [SMD]"]
  D1 = LTE-302 [package=lte-302]
  R1 = Resistor [tolerance=±5% resistance=220 package="2512 [SMD]"]
  R2 = Resistor [tolerance=±5% resistance=220 package="2512 [SMD]"]

nets:
  N1: Part1.D0/RX, U1.TXD
  GND: Part1.GND, U2.VSS, Light_Sensor1.GND
  5V: Part1.5V, U2.VDD, Light_Sensor1.Vcc
  N2: Part1.A4, U2.PWM_SDA, Light_Sensor1.SDA
  VCC: U1.VCC, YL-83_-_Control_Board2.VCC
  N3: U1.GPIO_2, YL-83_-_Control_Board2.DO
  GND_2: U1.GND, YL-83_-_Control_Board2.GND
  N4: U1.GPIO_4, R1.Pin_1
  N5: U1.GPIO_5, R2.Pin_1
  N6: U1.ADC_0, YL-83_-_Control_Board2.AO
  N7: YL-83_-_Detection_Board2.POS, YL-83_-_Control_Board2.POS
  N8: YL-83_-_Detection_Board2.NEG, YL-83_-_Control_Board2.NEG
  N9: U2.SCL_VZ, Light_Sensor1.SCL
  N10: LED1.cathode, D1.C

custom parts:
  YL-83 Rain Sensor - Detection Board: The YL-83 is a rain sensor that has more resistance when dry and less resistance when wet. The module runs at 5V.
  YL-83 Rain Sensor - Control Board: The YL-83 is a rain sensor that has more resistance when dry and less resistance when wet. The module runs at 5V.
