# Fritzing sketch skymonitor (saved by Fritzing 0.9.3b)

parts:
  Part1 = Arduino Nano (Rev3.0)
  U1 = ESP8266 WiFi Module [part_number=ESP8266]
  YL-83_-_Detection_Board2 = YL-83 Rain Sensor - Detection Board
  U2 = MLX90614 [package=to-39]
  Light_Sensor1 = Light Sensor
  YL-83_-_Control_Board2 = YL-83 Rain Sensor - Control Board

nets:
  N1: Part1.D1/TX, U1.RXD
  N2: Part1.D0/RX, U1.TXD
  GND: Part1.GND, U2.VSS, YL-83_-_Control_Board2.GND
  N3: Part1.D3, U2.SCL_VZ
  5V: Part1.5V, U2.VDD, YL-83_-_Control_Board2.VCC
  N4: Part1.A0, U2.PWM_SDA
  VCC: U1.VCC, Light_Sensor1.Vcc
  GND_2: U1.GND, Light_Sensor1.GND
  N5: U1.GPIO_4, Light_Sensor1.SDA
  N6: U1.GPIO_5, Light_Sensor1.SCL
  N7: YL-83_-_Detection_Board2.POS, YL-83_-_Control_Board2.POS
  N8: YL-83_-_Detection_Board2.NEG, YL-83_-_Control_Board2.NEG

custom parts:
  YL-83 Rain Sensor - Detection Board: The YL-83 is a rain sensor that has more resistance when dry and less resistance when wet. The module runs at 5V.
  YL-83 Rain Sensor - Control Board: The YL-83 is a rain sensor that has more resistance when dry and less resistance when wet. The module runs at 5V.
